// Logisim project full-adder.circ as structural Verilog: 1 circuit, main circuit Main
module Main (
  input  A,
  input  B,
  input  Cin,
  output Sum,
  output Cout
);

  wire AB, X1, XC;

  // XOR_Gate xor_1: pin names not known; wires that end beside it: A, B, X1
  and and_1 (AB, A, B);
  // XOR_Gate xor_2: pin names not known; wires that end beside it: X1, Cin, Sum
  and and_2 (XC, X1, Cin);
  or or_1 (Cout, AB, XC);
endmodule
